# Fritzing sketch Thermostat (saved by Fritzing 0.9.3b)
breadboards: 1

parts:
  WeMos_D1_Mini1 = WeMos D1 Mini
  Part1 = HTU21D Breakout
  U2 = RF-LINK_TX [package=rf-link_tx]

nets:
  3V3: WeMos_D1_Mini1.3V3, Part1.3.3V, U2.ANT
  N1: WeMos_D1_Mini1.D1, Part1.SCL
  N2: WeMos_D1_Mini1.D2, Part1.SDA
  N3: WeMos_D1_Mini1.D3, U2.DATA
  GND: Part1.GND, U2.GND

custom parts:
  HTU21D Breakout: This is a breadboard friendly breakout board for the Measurement Specialties high-precision, low-power digital humidity sensor.
